// Logisim project ALU.circ as structural Verilog: 1 circuit, main circuit main
module main (
  input  [15:0] INPUT_A,
  input  ZERO_A,
  input  NEGATE_A,
  input  [15:0] INPUT_B,
  input  [1:0] SELECT_MODE,
  input  ZERO_OUT,
  input  NEGATE_OUT,
  input  ZERO_B,
  input  NEGATE_B,
  output [15:0] out_10
);

  wire [15:0] ADD_OUT, AND_OUT, INA, INB, multiplexer_1_out, multiplexer_2_out, multiplexer_5_out,
       multiplexer_6_out, not_1_out, not_2_out, not_3_out, OR_OUT, XOR_OUT;

  Multiplexer #(.width(16)) multiplexer_1 (.in0(INPUT_A), .in1({16{1'b0}}), .out(multiplexer_1_out), .sel(ZERO_A));
  Multiplexer #(.width(16)) multiplexer_2 (.in0(INPUT_B), .in1({16{1'b0}}), .out(multiplexer_2_out), .sel(ZERO_B));
  assign not_1_out = ~multiplexer_1_out;  // NOT_Gate not_1, 16 bits wide
  assign not_2_out = ~multiplexer_2_out;  // NOT_Gate not_2, 16 bits wide
  Multiplexer #(.width(16)) multiplexer_3 (.in0(multiplexer_1_out), .in1(not_1_out), .out(INA), .sel(NEGATE_A));
  Multiplexer #(.width(16)) multiplexer_4 (.in0(multiplexer_2_out), .in1(not_2_out), .out(INB), .sel(NEGATE_B));
  assign AND_OUT = INA & INB;  // AND_Gate and_1, 16 bits wide
  assign OR_OUT = INA | INB;  // OR_Gate or_1, 16 bits wide
  assign XOR_OUT = INA ^ INB;  // XOR_Gate xor_1, 16 bits wide
  Adder #(.width(16)) adder_1 (.a(INA), .b(INB), .out(ADD_OUT));  // open: cin, cout
  Multiplexer #(.select(2), .width(16)) multiplexer_5 (
    .in0(AND_OUT), .in1(OR_OUT), .in2(XOR_OUT), .in3(ADD_OUT), .out(multiplexer_5_out), .sel(SELECT_MODE));
  Multiplexer #(.width(16)) multiplexer_6 (
    .in0(multiplexer_5_out), .in1({16{1'b0}}), .out(multiplexer_6_out), .sel(ZERO_OUT));
  assign not_3_out = ~multiplexer_6_out;  // NOT_Gate not_3, 16 bits wide
  Multiplexer #(.width(16)) multiplexer_7 (.in0(multiplexer_6_out), .in1(not_3_out), .out(out_10), .sel(NEGATE_OUT));

  // Notes on the sheet:
  //   INPUT_A
  //   INPUT_B
  //   AND
  //   OR
  //   XOR
  //   ADD
endmodule
